# Fritzing sketch fada (saved by Fritzing 0.9.10b)

parts:
  Componente1 = IMU Digital Combo Board 6DOF
  Mod1 = Amica NodeMCU DEVKIT 1.0
  U1 = LIPO-2000mAh [package=lipo-2000]
  S1 = Round Pushbutton
  TP1 = TP4056 [chip_label=TP4056 package="DIP (Dual Inline) [THT]"]

nets:
  N1: Componente1.3.3V, Mod1.pin1, Mod1.pin_10, S1.leg1
  N2: Componente1.GND, Mod1.pin2, Mod1.pin_9, Mod1.pin_29, TP1.pin6
  N3: Componente1.SDA, Mod1.pin_23
  N4: Componente1.SCL, Mod1.pin_24
  N5: Mod1.pin_15, S1.leg0
  N6: Mod1.pin_30, TP1.pin3
  N7: U1.+, TP1.pin4
  N8: U1.-, TP1.pin5

custom parts:
  TP4056: A DIP stand-in part for whatever IC you want. With 6 pins on a 300mil dual inline package (DIP) footprint.
