# Fritzing sketch sensor distancia - andy ' sketch (saved by Fritzing 0.9.10b)
breadboards: 1

parts:
  HC-SR04_Sensor_1 = HC-SR04 Ultrasonic Distance Sensor
  Componente1 = Arduino Uno (Rev3) - ICSP
  WeMos_D1_Mini_Relay_Shield1 = WeMos D1 Mini Relay Shield  # not connected

nets:
  VCC: HC-SR04_Sensor_1.VCC, Componente1.5V
  N1: HC-SR04_Sensor_1.TRIG, Componente1.D2
  N2: HC-SR04_Sensor_1.ECHO, Componente1.D3_PWM
  GND: HC-SR04_Sensor_1.GND, Componente1.GND
